// Digital circuit Encoder (s=2).dig as structural Verilog
module Encoder__s_2 (
  input  A_2,
  input  A_1,
  input  A_3,
  input  A_0,
  output S_0,
  output S_1
);

  or or_1 (S_0, A_1, A_3);
  or or_2 (S_1, A_2, A_3);
endmodule
